# Fritzing sketch ShuttleStride_circuit-diagram (saved by Fritzing 0.9.3b)

parts:
  M1 = fc-51 [package=THT]
  Part2 = NRF24L01+ Breakout Board
  LED3 = LEDs [package=led10mm]
  U1 = BATTERY-2 [package=battery-aa]
  U2 = BATTERY-2 [package=battery-aa]
  LED6 = LEDs [package=led10mm]
  LED2 = LEDs [package=led10mm]
  M2 = STM32F103C8T6 blue mini board

nets:
  N1: M1.pin1, M2.C14
  GND: M1.pin2, Part2.GND, LED3.C, U1.-1, LED6.C, LED2.C, M2.G, M2.GND
  VCC: M1.pin3, Part2.VCC, U2.+1, M2.3.3V, M2.3.3
  N2: Part2.CE, M2.B0
  N3: Part2.CS, M2.A4
  N4: Part2.SCK, M2.A5
  N5: Part2.MOSI, M2.A7
  N6: Part2.MISO, M2.A6
  N7: LED3.A, M2.B13
  N8: U1.+1, U2.-1
  N9: LED6.A, M2.B9
  N10: LED2.A, M2.A15

custom parts:
  STM32F103C8T6 blue mini board: Generic Blue Pill microcomputer module, available from Ebay and others. CPU STM32F103C8 72Mhz Flash: 64 KB/128 KB RAM: 20KB.
